# Fritzing sketch Fritzing dos motores circuito (saved by Fritzing 0.8.7b)
breadboards: 1

parts:
  Parte1 = Arduino Nano (Rev3.0)
  VCC1 = Battery
  IC1 = L293D [package=THT]
  Raspberry_Pi_B_rev1 = Raspberry Pi B rev2  # not connected
  M2 = DC Motor
  M1 = DC Motor

nets:
  N1: Parte1.RESET, VCC1.-, IC1.0V
  N2: Parte1.D5, IC1.Enable_2
  N3: Parte1.D6, IC1.In_3
  N4: Parte1.D7, IC1.In_4
  N5: Parte1.D8, IC1.Enable_1
  N6: Parte1.D9, IC1.In_1
  N7: Parte1.D10, IC1.In_2
  N8: Parte1.5V, IC1.+V
  N9: VCC1.+, IC1.+Vmotor
  N10: IC1.Out_1_(_Controlled_by_Enable_1_), M2.pin_2
  N11: IC1.Out_2_(_Controlled_by_Enable_1_), M2.pin_1
  N12: IC1.Out_3_(_Controlled_by_Enable_2_), M1.pin_2
  N13: IC1.Out_4_(_Controlled_by_Enable_2_), M1.pin_1
